# Fritzing sketch AC_Controller (saved by Fritzing 0.9.0b)
circuit board: 8.46667cm x 5.64444cm
breadboards: 1

parts:
  Arduino = Arduino Uno (Rev3)
  LED = LED - 5mm [color="Infrared (940nm)" package="5 mm [THT]"]
  DHT = DHT11 Humitidy and Temperature Sensor

nets:
  N1: Arduino.A0, DHT.DATA
  GND: Arduino.GND, LED.cathode, DHT.GND
  N2: Arduino.D3_PWM, LED.anode
  5V: Arduino.5V, DHT.VDD

custom parts:
  DHT11 Humitidy and Temperature Sensor: DHT11 Humidity and Temperature Sensor
